// Logisim project LUT_v2.circ as structural Verilog: 4 circuits, main circuit main
module main (
  output out_1,
  output out_2,
  output out_3,
  output out_4,
  output out_5,
  output out_6,
  output [7:0] out_7,
  output [7:0] out_8,
  output [1:0] SC1,
  output [1:0] SC1_2,
  output [1:0] SC2,
  output [1:0] SC2_2,
  output [1:0] SC3,
  output [1:0] SC3_2,
  output out_15,
  output out_16,
  output out_17,
  output out_18,
  output out_19,
  output out_20,
  output [7:0] out_21,
  output [7:0] out_22,
  output [1:0] SC1_3,
  output [1:0] SC1_4,
  output [1:0] SC2_3,
  output [1:0] SC2_4,
  output [1:0] SC3_3,
  output [1:0] SC3_4
);

  wire [3:1] L0_y, undriven, undriven_2, undriven_3;

  lut_switch L0 (
    .Config_bits(out_7), .SM1({undriven, out_3}), .SM2({undriven, out_2}), .SM3({undriven, out_1}),
    .SC1(SC1), .SC2(SC2), .SC3(SC3), .Y(L0_y[1]));
  lut_switch L2 (
    .Config_bits(out_21), .SM1({undriven_2, out_17}), .SM2({undriven_2, out_16}), .SM3({undriven_2, out_15}),
    .SC1(SC1_3), .SC2(SC2_3), .SC3(SC3_3), .Y(L0_y[2]));
  lut_switch L1 (
    .Config_bits(out_8), .SM1({L0_y, out_6}), .SM2({L0_y, out_5}), .SM3({L0_y, out_4}), .SC1(SC1_2),
    .SC2(SC2_2), .SC3(SC3_2), .Y(undriven[2]));
  lut_switch L3 (
    .Config_bits(out_22), .SM1({undriven_3, out_20}), .SM2({undriven_3, out_19}), .SM3({undriven_3, out_18}),
    .SC1(SC1_4), .SC2(SC2_4), .SC3(SC3_4), .Y(L0_y[3]));
endmodule

module LUT_v2 (
  input  [7:0] Config_bits,
  input  IP1,
  input  IP2,
  input  IP3,
  output out_5
);

  Multiplexer #(.select(3), .enable("false")) multiplexer_1 (
    .in0(Config_bits[0]), .in1(Config_bits[1]), .in2(Config_bits[2]), .in3(Config_bits[3]),
    .in4(Config_bits[4]), .in5(Config_bits[5]), .in6(Config_bits[6]), .in7(Config_bits[7]), .out(out_5),
    .sel({IP1, IP2, IP3}));
endmodule

module Switch_matrix (
  input  [3:0] SM,
  input  [1:0] SC,
  output out_3
);

  Multiplexer #(.select(2), .enable("false")) multiplexer_1 (
    .in0(SM[0]), .in1(SM[1]), .in2(SM[2]), .in3(SM[3]), .out(out_3), .sel(SC));
endmodule

module lut_switch (
  input  [7:0] Config_bits,
  input  [3:0] SM1,
  input  [3:0] SM2,
  input  [3:0] SM3,
  input  [1:0] SC1,
  input  [1:0] SC2,
  input  [1:0] SC3,
  output Y
);

  wire switch_matrix_1_out_3, switch_matrix_2_out_3, switch_matrix_3_out_3;

  Switch_matrix switch_matrix_1 (.SM(SM1), .SC(SC1), .out_3(switch_matrix_1_out_3));
  Switch_matrix switch_matrix_2 (.SM(SM2), .SC(SC2), .out_3(switch_matrix_2_out_3));
  Switch_matrix switch_matrix_3 (.SM(SM3), .SC(SC3), .out_3(switch_matrix_3_out_3));
  LUT_v2 lut_v2_1 (
    .Config_bits(Config_bits), .IP1(switch_matrix_1_out_3), .IP2(switch_matrix_2_out_3),
    .IP3(switch_matrix_3_out_3), .out_5(Y));
endmodule
